// Logisim project Single Cycle Datapath.circ as structural Verilog: 5 circuits, main circuit main
module main (
  input  in_1,
  output [31:0] out_2,
  output [3:0] out_3,
  output [4:0] out_4,
  output [4:0] out_5,
  output [4:0] out_6,
  output [2:0] out_7,
  output [21:0] out_8,
  output [21:0] out_9,
  output [31:0] out_10,
  output [31:0] out_11,
  output out_12,
  output [31:0] out_13,
  output [7:0] out_14,
  output [17:0] out_15,
  output out_16,
  output out_17,
  output [1:0] out_18,
  output [31:0] out_19
);

  wire alu_1_negative, alu_1_zero_signal, and_1_out, Clock, control_unit_1_alusrc, control_unit_1_memread,
       control_unit_1_memtoreg, control_unit_1_memwrite, control_unit_1_regdest, control_unit_1_regwrite;
  wire [4:0] multiplexer_4_out;
  wire [21:0] adder_1_out, bit_extender_1_out, bit_extender_2_out, multiplexer_1_out, multiplexer_2_out;
  wire [31:0] bit_extender_3_out, bit_extender_4_out, multiplexer_3_out, multiplexer_6_out;

  Adder #(.width(22)) adder_1 (.a(out_8), .b(bit_extender_1_out), .out(adder_1_out));  // open: cin, cout
  and and_1 (and_1_out, alu_1_zero_signal, out_12);
  assign bit_extender_1_out = {{14{1'b0}}, {out_6, out_7}};  // Bit_Extender bit_extender_1
  Multiplexer #(.width(22), .enable("false")) multiplexer_1 (
    .in0(out_9), .in1(adder_1_out), .out(multiplexer_1_out), .sel(and_1_out));
  assign bit_extender_2_out = {{4{1'b0}}, {out_4, out_5, out_6, out_7}};  // Bit_Extender bit_extender_2
  Clock clock_1 (.out(Clock));
  Multiplexer #(.width(22), .enable("false")) multiplexer_2 (
    .in0(multiplexer_1_out), .in1(bit_extender_2_out), .out(multiplexer_2_out), .sel(out_16));
  Register #(.width(22)) register_1 (.D(multiplexer_2_out), .Q(out_8), .clk(Clock), .clr(in_1));  // open: en
  Adder #(.width(22)) adder_2 (.a(22'h1), .b(out_8), .out(out_9));  // open: cin, cout
  ROM #(.addrWidth(22), .dataWidth(22)) rom_1 (.addr(out_8), .data({out_3, out_4, out_5, out_6, out_7}));  // open: sel
  Control_Unit control_unit_1 (
    .OpCode(out_3), .AluOp(out_18), .RegDest(control_unit_1_regdest), .Jump(out_16), .Branch(out_12),
    .MemRead(control_unit_1_memread), .MemToReg(control_unit_1_memtoreg), .MemWrite(control_unit_1_memwrite),
    .AluSrc(control_unit_1_alusrc), .RegWrite(control_unit_1_regwrite), .Slt(out_17));
  Multiplexer #(.width(32), .enable("false")) multiplexer_3 (
    .in0(multiplexer_6_out), .in1(out_11), .out(multiplexer_3_out), .sel(control_unit_1_memtoreg));
  Multiplexer #(.width(5), .enable("false")) multiplexer_4 (
    .in0(out_6), .in1(out_5), .out(multiplexer_4_out), .sel(control_unit_1_regdest));
  Register_file register_file_1 (
    .Write_Data(multiplexer_3_out), .Clock(Clock), .Read_Data_1(out_2), .Read_Data_2(out_19),
    .Write(control_unit_1_regwrite), .Write_Register_Address(multiplexer_4_out),
    .Read_Register_Address_1(out_4), .Read_Register_Address_2(out_5));
  assign bit_extender_3_out = {{24{1'b0}}, {out_6, out_7}};  // Bit_Extender bit_extender_3
  Multiplexer #(.width(32), .enable("false")) multiplexer_5 (
    .in0(out_19), .in1(bit_extender_3_out), .out(out_13), .sel(control_unit_1_alusrc));
  ALU alu_1 (
    .Shift_Amount(out_7), .Result(out_10), .Zero_Signal(alu_1_zero_signal), .Negative(alu_1_negative),
    .B(out_13), .A(out_2), .ALUop(out_18));
  assign bit_extender_4_out = {{31{1'b0}}, alu_1_negative};  // Bit_Extender bit_extender_4
  Multiplexer #(.width(32), .enable("false")) multiplexer_6 (
    .in0(out_10), .in1(bit_extender_4_out), .out(multiplexer_6_out), .sel(out_17));
  RAM #(.addrWidth(16), .dataWidth(16), .bus("separate")) ram_1 (
    .addr(out_10[15:0]), .din(out_19[15:0]), .data(out_11[15:0]), .str(control_unit_1_memwrite), .clk(Clock),
    .ld(control_unit_1_memread));  // open: sel, clr
  RAM #(.addrWidth(16), .dataWidth(16), .bus("separate")) ram_2 (
    .addr(out_10[31:16]), .din(out_19[31:16]), .data(out_11[31:16]), .str(control_unit_1_memwrite),
    .clk(Clock), .ld(control_unit_1_memread));  // open: sel, clr

  assign out_14 = {out_6, out_7};
  assign out_15 = {out_4, out_5, out_6, out_7};

  // Other names for the same wires on the sheet: Address[17:0] = {out_4, out_5, out_6, out_7};
  //   Immediate[7:0] = {out_6, out_7}; shamt[2:0] = out_7; rd[4:0] = out_6; rt[4:0] = out_5; rs[4:0] = out_4;
  //   OpCode[3:0] = out_3; A[31:0] = out_2; AluOp[1:0] = out_18; B[31:0] = out_13; Branch = out_12; Jump = out_16;
  //   MemData[31:0] = out_19; Next_Address[21:0] = out_9; Present_Address[21:0] = out_8; Reset = in_1;
  //   Result_from_ALU[31:0] = out_10; Result_from_RAM[31:0] = out_11; Slt = out_17

  // Notes on the sheet:
  //   contents of rom_1 (hex, n*v repeats v):
  //   0 42101 4630b 1c2304 4110 42102 280003
  //   Address
  //   32 bit Architecture
  //   22 bit Instructions
endmodule

module ALU (
  input  [31:0] B,
  input  [31:0] A,
  input  [2:0] Shift_Amount,
  input  [1:0] ALUop,
  output [31:0] Result,
  output Zero_Signal,
  output Negative
);

  wire [4:0] bit_extender_1_out;
  wire [31:0] adder_1_out, shifter_1_out, subtractor_1_out, xnor_1_out;

  assign bit_extender_1_out = {{2{1'b0}}, Shift_Amount};  // Bit_Extender bit_extender_1
  Adder #(.width(32)) adder_1 (.a(A), .b(B), .out(adder_1_out));  // open: cin, cout
  Subtractor #(.width(32)) subtractor_1 (.a(A), .b(B), .out(subtractor_1_out));  // open: bin, bout
  Shifter #(.width(32), .shift("lr")) shifter_1 (.in(A), .\dist (bit_extender_1_out), .out(shifter_1_out));
  assign xnor_1_out = ~(A ^ B);  // XNOR_Gate xnor_1, 32 bits wide
  Multiplexer #(.select(2), .width(32), .enable("false")) multiplexer_1 (
    .in0(adder_1_out), .in1(subtractor_1_out), .in2(xnor_1_out), .in3(shifter_1_out),
    .out({Negative, Result[30:0]}), .sel(ALUop));
  nor nor_1 (Zero_Signal, Result[0], Result[1], Result[2], Result[3], Result[4], Result[5], Result[6], Result[7], Result[8], Result[9], Result[10], Result[11], Result[12], Result[13], Result[14], Result[15], Result[16], Result[17], Result[18], Result[19], Result[20], Result[21], Result[22], Result[23], Result[24], Result[25], Result[26], Result[27], Result[28], Result[29], Result[30], Negative);

  assign Result[31] = Negative;
endmodule

module _32_bit_register (
  input  [31:0] Data,
  input  Clock,
  input  Enable,
  output [31:0] Output
);

  D_Flip_Flop d_ff_1 (.clk(Clock), .D(Data[0]), .Q(Output[0]), .en(Enable));  // open: Qn, preset, reset
  D_Flip_Flop d_ff_2 (.clk(Clock), .D(Data[1]), .Q(Output[1]), .en(Enable));  // open: Qn, preset, reset
  D_Flip_Flop d_ff_3 (.clk(Clock), .D(Data[2]), .Q(Output[2]), .en(Enable));  // open: Qn, preset, reset
  D_Flip_Flop d_ff_4 (.clk(Clock), .D(Data[3]), .Q(Output[3]), .en(Enable));  // open: Qn, preset, reset
  D_Flip_Flop d_ff_5 (.clk(Clock), .D(Data[4]), .Q(Output[4]), .en(Enable));  // open: Qn, preset, reset
  D_Flip_Flop d_ff_6 (.clk(Clock), .D(Data[5]), .Q(Output[5]), .en(Enable));  // open: Qn, preset, reset
  D_Flip_Flop d_ff_7 (.clk(Clock), .D(Data[6]), .Q(Output[6]), .en(Enable));  // open: Qn, preset, reset
  D_Flip_Flop d_ff_8 (.clk(Clock), .D(Data[7]), .Q(Output[7]), .en(Enable));  // open: Qn, preset, reset
  D_Flip_Flop d_ff_9 (.clk(Clock), .D(Data[8]), .Q(Output[8]), .en(Enable));  // open: Qn, preset, reset
  D_Flip_Flop d_ff_10 (.clk(Clock), .D(Data[9]), .Q(Output[9]), .en(Enable));  // open: Qn, preset, reset
  D_Flip_Flop d_ff_11 (.clk(Clock), .D(Data[10]), .Q(Output[10]), .en(Enable));  // open: Qn, preset, reset
  D_Flip_Flop d_ff_12 (.clk(Clock), .D(Data[11]), .Q(Output[11]), .en(Enable));  // open: Qn, preset, reset
  D_Flip_Flop d_ff_13 (.clk(Clock), .D(Data[12]), .Q(Output[12]), .en(Enable));  // open: Qn, preset, reset
  D_Flip_Flop d_ff_14 (.clk(Clock), .D(Data[13]), .Q(Output[13]), .en(Enable));  // open: Qn, preset, reset
  D_Flip_Flop d_ff_15 (.clk(Clock), .D(Data[14]), .Q(Output[14]), .en(Enable));  // open: Qn, preset, reset
  D_Flip_Flop d_ff_16 (.clk(Clock), .D(Data[15]), .Q(Output[15]), .en(Enable));  // open: Qn, preset, reset
  D_Flip_Flop d_ff_17 (.clk(Clock), .D(Data[16]), .Q(Output[16]), .en(Enable));  // open: Qn, preset, reset
  D_Flip_Flop d_ff_18 (.clk(Clock), .D(Data[17]), .Q(Output[17]), .en(Enable));  // open: Qn, preset, reset
  D_Flip_Flop d_ff_19 (.clk(Clock), .D(Data[18]), .Q(Output[18]), .en(Enable));  // open: Qn, preset, reset
  D_Flip_Flop d_ff_20 (.clk(Clock), .D(Data[19]), .Q(Output[19]), .en(Enable));  // open: Qn, preset, reset
  D_Flip_Flop d_ff_21 (.clk(Clock), .D(Data[20]), .Q(Output[20]), .en(Enable));  // open: Qn, preset, reset
  D_Flip_Flop d_ff_22 (.clk(Clock), .D(Data[21]), .Q(Output[21]), .en(Enable));  // open: Qn, preset, reset
  D_Flip_Flop d_ff_23 (.clk(Clock), .D(Data[22]), .Q(Output[22]), .en(Enable));  // open: Qn, preset, reset
  D_Flip_Flop d_ff_24 (.clk(Clock), .D(Data[23]), .Q(Output[23]), .en(Enable));  // open: Qn, preset, reset
  D_Flip_Flop d_ff_25 (.clk(Clock), .D(Data[24]), .Q(Output[24]), .en(Enable));  // open: Qn, preset, reset
  D_Flip_Flop d_ff_26 (.clk(Clock), .D(Data[25]), .Q(Output[25]), .en(Enable));  // open: Qn, preset, reset
  D_Flip_Flop d_ff_27 (.clk(Clock), .D(Data[26]), .Q(Output[26]), .en(Enable));  // open: Qn, preset, reset
  D_Flip_Flop d_ff_28 (.clk(Clock), .D(Data[27]), .Q(Output[27]), .en(Enable));  // open: Qn, preset, reset
  D_Flip_Flop d_ff_29 (.clk(Clock), .D(Data[28]), .Q(Output[28]), .en(Enable));  // open: Qn, preset, reset
  D_Flip_Flop d_ff_30 (.clk(Clock), .D(Data[29]), .Q(Output[29]), .en(Enable));  // open: Qn, preset, reset
  D_Flip_Flop d_ff_31 (.clk(Clock), .D(Data[30]), .Q(Output[30]), .en(Enable));  // open: Qn, preset, reset
  D_Flip_Flop d_ff_32 (.clk(Clock), .D(Data[31]), .Q(Output[31]), .en(Enable));  // open: Qn, preset, reset
endmodule

module Register_file (
  input  [31:0] Write_Data,
  input  Clock,
  input  Write,
  input  [4:0] Write_Register_Address,
  input  [4:0] Read_Register_Address_1,
  input  [4:0] Read_Register_Address_2,
  output [31:0] Read_Data_1,
  output [31:0] Read_Data_2
);

  wire decoder_1_out0, decoder_1_out1, decoder_1_out2, decoder_1_out3, decoder_1_out4, decoder_1_out5,
       decoder_1_out6, decoder_1_out7, decoder_1_out8, decoder_1_out9, decoder_1_out10, decoder_1_out11,
       decoder_1_out12, decoder_1_out13, decoder_1_out14, decoder_1_out15, decoder_1_out16, decoder_1_out17,
       decoder_1_out18, decoder_1_out19, decoder_1_out20, decoder_1_out21, decoder_1_out22, decoder_1_out23,
       decoder_1_out24, decoder_1_out25, decoder_1_out26, decoder_1_out27, decoder_1_out28, decoder_1_out29,
       decoder_1_out30, decoder_1_out31;
  wire [31:0] n32_bit_register_1_output, n32_bit_register_2_output, n32_bit_register_3_output,
       n32_bit_register_4_output, n32_bit_register_5_output, n32_bit_register_6_output,
       n32_bit_register_7_output, n32_bit_register_8_output, n32_bit_register_9_output,
       n32_bit_register_10_output, n32_bit_register_11_output, n32_bit_register_12_output,
       n32_bit_register_13_output, n32_bit_register_14_output, n32_bit_register_15_output,
       n32_bit_register_16_output, n32_bit_register_17_output, n32_bit_register_18_output,
       n32_bit_register_19_output, n32_bit_register_20_output, n32_bit_register_21_output,
       n32_bit_register_22_output, n32_bit_register_23_output, n32_bit_register_24_output,
       n32_bit_register_25_output, n32_bit_register_26_output, n32_bit_register_27_output,
       n32_bit_register_28_output, n32_bit_register_29_output, n32_bit_register_30_output,
       n32_bit_register_31_output, n32_bit_register_32_output;

  Decoder #(.select(5), .disabled(0)) decoder_1 (
    .out0(decoder_1_out0), .out1(decoder_1_out1), .out2(decoder_1_out2), .out3(decoder_1_out3),
    .out4(decoder_1_out4), .out5(decoder_1_out5), .out6(decoder_1_out6), .out7(decoder_1_out7),
    .out8(decoder_1_out8), .out9(decoder_1_out9), .out10(decoder_1_out10), .out11(decoder_1_out11),
    .out12(decoder_1_out12), .out13(decoder_1_out13), .out14(decoder_1_out14), .out15(decoder_1_out15),
    .out16(decoder_1_out16), .out17(decoder_1_out17), .out18(decoder_1_out18), .out19(decoder_1_out19),
    .out20(decoder_1_out20), .out21(decoder_1_out21), .out22(decoder_1_out22), .out23(decoder_1_out23),
    .out24(decoder_1_out24), .out25(decoder_1_out25), .out26(decoder_1_out26), .out27(decoder_1_out27),
    .out28(decoder_1_out28), .out29(decoder_1_out29), .out30(decoder_1_out30), .out31(decoder_1_out31),
    .sel(Write_Register_Address), .en(Write));
  _32_bit_register u_32_bit_register_1 (
    .Data(Write_Data), .Clock(Clock), .Enable(decoder_1_out0), .Output(n32_bit_register_1_output));
  _32_bit_register u_32_bit_register_2 (
    .Data(Write_Data), .Clock(Clock), .Enable(decoder_1_out4), .Output(n32_bit_register_2_output));
  _32_bit_register u_32_bit_register_3 (
    .Data(Write_Data), .Clock(Clock), .Enable(decoder_1_out8), .Output(n32_bit_register_3_output));
  _32_bit_register u_32_bit_register_4 (
    .Data(Write_Data), .Clock(Clock), .Enable(decoder_1_out12), .Output(n32_bit_register_4_output));
  _32_bit_register u_32_bit_register_5 (
    .Data(Write_Data), .Clock(Clock), .Enable(decoder_1_out16), .Output(n32_bit_register_5_output));
  _32_bit_register u_32_bit_register_6 (
    .Data(Write_Data), .Clock(Clock), .Enable(decoder_1_out20), .Output(n32_bit_register_6_output));
  _32_bit_register u_32_bit_register_7 (
    .Data(Write_Data), .Clock(Clock), .Enable(decoder_1_out24), .Output(n32_bit_register_7_output));
  _32_bit_register u_32_bit_register_8 (
    .Data(Write_Data), .Clock(Clock), .Enable(decoder_1_out28), .Output(n32_bit_register_8_output));
  _32_bit_register u_32_bit_register_9 (
    .Data(Write_Data), .Clock(Clock), .Enable(decoder_1_out1), .Output(n32_bit_register_9_output));
  _32_bit_register u_32_bit_register_10 (
    .Data(Write_Data), .Clock(Clock), .Enable(decoder_1_out5), .Output(n32_bit_register_10_output));
  _32_bit_register u_32_bit_register_11 (
    .Data(Write_Data), .Clock(Clock), .Enable(decoder_1_out9), .Output(n32_bit_register_11_output));
  _32_bit_register u_32_bit_register_12 (
    .Data(Write_Data), .Clock(Clock), .Enable(decoder_1_out13), .Output(n32_bit_register_12_output));
  _32_bit_register u_32_bit_register_13 (
    .Data(Write_Data), .Clock(Clock), .Enable(decoder_1_out17), .Output(n32_bit_register_13_output));
  _32_bit_register u_32_bit_register_14 (
    .Data(Write_Data), .Clock(Clock), .Enable(decoder_1_out21), .Output(n32_bit_register_14_output));
  _32_bit_register u_32_bit_register_15 (
    .Data(Write_Data), .Clock(Clock), .Enable(decoder_1_out25), .Output(n32_bit_register_15_output));
  _32_bit_register u_32_bit_register_16 (
    .Data(Write_Data), .Clock(Clock), .Enable(decoder_1_out29), .Output(n32_bit_register_16_output));
  _32_bit_register u_32_bit_register_17 (
    .Data(Write_Data), .Clock(Clock), .Enable(decoder_1_out2), .Output(n32_bit_register_17_output));
  _32_bit_register u_32_bit_register_18 (
    .Data(Write_Data), .Clock(Clock), .Enable(decoder_1_out6), .Output(n32_bit_register_18_output));
  _32_bit_register u_32_bit_register_19 (
    .Data(Write_Data), .Clock(Clock), .Enable(decoder_1_out10), .Output(n32_bit_register_19_output));
  _32_bit_register u_32_bit_register_20 (
    .Data(Write_Data), .Clock(Clock), .Enable(decoder_1_out14), .Output(n32_bit_register_20_output));
  _32_bit_register u_32_bit_register_21 (
    .Data(Write_Data), .Clock(Clock), .Enable(decoder_1_out18), .Output(n32_bit_register_21_output));
  _32_bit_register u_32_bit_register_22 (
    .Data(Write_Data), .Clock(Clock), .Enable(decoder_1_out22), .Output(n32_bit_register_22_output));
  _32_bit_register u_32_bit_register_23 (
    .Data(Write_Data), .Clock(Clock), .Enable(decoder_1_out26), .Output(n32_bit_register_23_output));
  _32_bit_register u_32_bit_register_24 (
    .Data(Write_Data), .Clock(Clock), .Enable(decoder_1_out30), .Output(n32_bit_register_24_output));
  _32_bit_register u_32_bit_register_25 (
    .Data(Write_Data), .Clock(Clock), .Enable(decoder_1_out3), .Output(n32_bit_register_25_output));
  _32_bit_register u_32_bit_register_26 (
    .Data(Write_Data), .Clock(Clock), .Enable(decoder_1_out7), .Output(n32_bit_register_26_output));
  _32_bit_register u_32_bit_register_27 (
    .Data(Write_Data), .Clock(Clock), .Enable(decoder_1_out11), .Output(n32_bit_register_27_output));
  _32_bit_register u_32_bit_register_28 (
    .Data(Write_Data), .Clock(Clock), .Enable(decoder_1_out15), .Output(n32_bit_register_28_output));
  _32_bit_register u_32_bit_register_29 (
    .Data(Write_Data), .Clock(Clock), .Enable(decoder_1_out19), .Output(n32_bit_register_29_output));
  _32_bit_register u_32_bit_register_30 (
    .Data(Write_Data), .Clock(Clock), .Enable(decoder_1_out23), .Output(n32_bit_register_30_output));
  _32_bit_register u_32_bit_register_31 (
    .Data(Write_Data), .Clock(Clock), .Enable(decoder_1_out27), .Output(n32_bit_register_31_output));
  _32_bit_register u_32_bit_register_32 (
    .Data(Write_Data), .Clock(Clock), .Enable(decoder_1_out31), .Output(n32_bit_register_32_output));
  Multiplexer #(.select(5), .width(32), .enable("false")) multiplexer_1 (
    .in0(n32_bit_register_1_output), .in1(n32_bit_register_9_output), .in2(n32_bit_register_17_output),
    .in3(n32_bit_register_25_output), .in4(n32_bit_register_2_output), .in5(n32_bit_register_10_output),
    .in6(n32_bit_register_18_output), .in7(n32_bit_register_26_output), .in8(n32_bit_register_3_output),
    .in9(n32_bit_register_11_output), .in10(n32_bit_register_19_output), .in11(n32_bit_register_27_output),
    .in12(n32_bit_register_4_output), .in13(n32_bit_register_12_output), .in14(n32_bit_register_20_output),
    .in15(n32_bit_register_28_output), .in16(n32_bit_register_5_output), .in17(n32_bit_register_13_output),
    .in18(n32_bit_register_21_output), .in19(n32_bit_register_29_output), .in20(n32_bit_register_6_output),
    .in21(n32_bit_register_14_output), .in22(n32_bit_register_22_output), .in23(n32_bit_register_30_output),
    .in24(n32_bit_register_7_output), .in25(n32_bit_register_15_output), .in26(n32_bit_register_23_output),
    .in27(n32_bit_register_31_output), .in28(n32_bit_register_8_output), .in29(n32_bit_register_16_output),
    .in30(n32_bit_register_24_output), .in31(n32_bit_register_32_output), .out(Read_Data_1),
    .sel(Read_Register_Address_1));
  Multiplexer #(.select(5), .width(32), .enable("false")) multiplexer_2 (
    .in0(n32_bit_register_1_output), .in1(n32_bit_register_9_output), .in2(n32_bit_register_17_output),
    .in3(n32_bit_register_25_output), .in4(n32_bit_register_2_output), .in5(n32_bit_register_10_output),
    .in6(n32_bit_register_18_output), .in7(n32_bit_register_26_output), .in8(n32_bit_register_3_output),
    .in9(n32_bit_register_11_output), .in10(n32_bit_register_19_output), .in11(n32_bit_register_27_output),
    .in12(n32_bit_register_4_output), .in13(n32_bit_register_12_output), .in14(n32_bit_register_20_output),
    .in15(n32_bit_register_28_output), .in16(n32_bit_register_5_output), .in17(n32_bit_register_13_output),
    .in18(n32_bit_register_21_output), .in19(n32_bit_register_29_output), .in20(n32_bit_register_6_output),
    .in21(n32_bit_register_14_output), .in22(n32_bit_register_22_output), .in23(n32_bit_register_30_output),
    .in24(n32_bit_register_7_output), .in25(n32_bit_register_15_output), .in26(n32_bit_register_23_output),
    .in27(n32_bit_register_31_output), .in28(n32_bit_register_8_output), .in29(n32_bit_register_16_output),
    .in30(n32_bit_register_24_output), .in31(n32_bit_register_32_output), .out(Read_Data_2),
    .sel(Read_Register_Address_2));
endmodule

module Control_Unit (
  input  [3:0] OpCode,
  output [1:0] AluOp,
  output RegDest,
  output Jump,
  output Branch,
  output MemRead,
  output MemToReg,
  output MemWrite,
  output AluSrc,
  output RegWrite,
  output Slt
);

  wire nand_1_out, nand_2_out, nand_3_out, nand_4_out, nand_5_out, nand_6_out, nand_7_out, nand_8_out,
       nand_9_out, nand_10_out, nand_11_out, nand_12_out, nand_13_out, nand_14_out, nand_15_out, nand_16_out,
       nand_17_out, nand_18_out, nand_19_out, nand_20_out, nand_21_out, nand_22_out, nand_23_out,
       nand_24_out, nand_25_out, nand_26_out, nand_27_out, nand_28_out, nand_29_out, nand_30_out,
       nand_31_out, nand_32_out, nand_33_out, nand_34_out, nand_35_out, nand_36_out, nand_37_out,
       nand_38_out, nand_39_out, nand_40_out, nand_41_out, nand_42_out, nand_43_out, nand_44_out,
       nand_45_out, nand_46_out, nand_47_out, nand_48_out, nand_49_out, nand_50_out, nand_51_out,
       nand_54_out, nand_55_out, nand_56_out, nand_58_out, nand_61_out;

  nand nand_1 (nand_1_out, OpCode[3], OpCode[3]);
  nand nand_2 (nand_2_out, OpCode[0], OpCode[0]);
  nand nand_3 (nand_3_out, OpCode[2], OpCode[2]);
  nand nand_4 (nand_4_out, OpCode[1], OpCode[1]);
  nand nand_5 (nand_5_out, OpCode[2], OpCode[2]);
  nand nand_6 (nand_6_out, OpCode[0], OpCode[0]);
  nand nand_7 (nand_7_out, OpCode[3], OpCode[3]);
  nand nand_8 (nand_8_out, OpCode[2], OpCode[2]);
  nand nand_9 (nand_9_out, OpCode[3], OpCode[3]);
  nand nand_10 (nand_10_out, OpCode[2], OpCode[2]);
  nand nand_11 (nand_11_out, OpCode[1], OpCode[1]);
  nand nand_12 (nand_12_out, OpCode[3], OpCode[3]);
  nand nand_13 (nand_13_out, OpCode[3], OpCode[3]);
  nand nand_14 (nand_14_out, OpCode[1], OpCode[1]);
  nand nand_15 (nand_15_out, OpCode[2], OpCode[2]);
  nand nand_16 (nand_16_out, OpCode[0], OpCode[0]);
  nand nand_17 (nand_17_out, OpCode[3], OpCode[3]);
  nand nand_18 (nand_18_out, OpCode[3], OpCode[3]);
  nand nand_19 (nand_19_out, OpCode[1], OpCode[1]);
  nand nand_20 (nand_20_out, OpCode[0], OpCode[0]);
  nand nand_21 (nand_21_out, OpCode[3], OpCode[3]);
  nand nand_22 (nand_22_out, OpCode[1], OpCode[1]);
  nand nand_23 (nand_23_out, OpCode[3], OpCode[3]);
  nand nand_24 (nand_24_out, OpCode[1], OpCode[1]);
  nand nand_25 (nand_25_out, OpCode[3], OpCode[3]);
  nand nand_26 (nand_26_out, OpCode[2], OpCode[2]);
  nand nand_27 (nand_27_out, OpCode[3], OpCode[3]);
  nand nand_28 (nand_28_out, OpCode[1], OpCode[1]);
  nand nand_29 (nand_29_out, OpCode[3], OpCode[3]);
  nand nand_30 (nand_30_out, OpCode[2], OpCode[2]);
  nand nand_31 (nand_31_out, OpCode[3], OpCode[3]);
  nand nand_32 (nand_32_out, OpCode[0], OpCode[0]);
  nand nand_33 (nand_33_out, OpCode[2], OpCode[2]);
  nand nand_34 (nand_34_out, OpCode[1], OpCode[1]);
  nand nand_35 (nand_35_out, OpCode[2], OpCode[2]);
  nand nand_36 (nand_36_out, OpCode[1], OpCode[1]);
  nand nand_37 (nand_37_out, OpCode[0], OpCode[0]);
  nand nand_38 (nand_38_out, nand_7_out, nand_8_out, OpCode[1]);
  nand nand_39 (nand_39_out, nand_9_out, OpCode[1], OpCode[0]);
  nand nand_40 (nand_40_out, OpCode[3], nand_10_out, nand_11_out);
  nand nand_41 (nand_41_out, nand_12_out, OpCode[0]);
  nand nand_42 (nand_42_out, nand_13_out, OpCode[2], nand_14_out);
  nand nand_43 (nand_43_out, nand_21_out, OpCode[2], nand_22_out);
  nand nand_44 (nand_44_out, nand_25_out, nand_26_out, OpCode[0]);
  nand nand_45 (nand_45_out, nand_27_out, OpCode[2], nand_28_out);
  nand nand_46 (nand_46_out, nand_29_out, nand_30_out);
  nand nand_47 (nand_47_out, nand_31_out, nand_32_out);
  nand nand_48 (nand_48_out, nand_33_out, nand_34_out);
  nand nand_49 (nand_49_out, nand_1_out, OpCode[2], OpCode[1], nand_2_out);
  nand nand_50 (nand_50_out, OpCode[3], nand_3_out, nand_4_out, OpCode[0]);
  nand nand_51 (nand_51_out, OpCode[3], nand_5_out, OpCode[1], nand_6_out);
  nand nand_52 (AluOp[0], nand_38_out, nand_39_out, nand_40_out);
  nand nand_53 (RegDest, nand_41_out, nand_42_out);
  nand nand_54 (nand_54_out, OpCode[3], nand_15_out, OpCode[1], nand_16_out);
  nand nand_55 (nand_55_out, nand_17_out, OpCode[2], OpCode[1], OpCode[0]);
  nand nand_56 (nand_56_out, nand_18_out, OpCode[2], nand_19_out, nand_20_out);
  nand nand_57 (MemToReg, nand_43_out, nand_43_out);
  nand nand_58 (nand_58_out, nand_23_out, OpCode[2], nand_24_out, OpCode[0]);
  nand nand_59 (AluSrc, nand_44_out, nand_45_out);
  nand nand_60 (RegWrite, nand_46_out, nand_47_out, nand_48_out);
  nand nand_61 (nand_61_out, OpCode[3], nand_35_out, nand_36_out, nand_37_out);
  nand nand_62 (AluOp[1], nand_49_out, nand_50_out, nand_51_out);
  nand nand_63 (Jump, nand_54_out, nand_54_out);
  nand nand_64 (Branch, nand_55_out, nand_55_out);
  nand nand_65 (MemRead, nand_56_out, nand_56_out);
  nand nand_66 (MemWrite, nand_58_out, nand_58_out);
  nand nand_67 (Slt, nand_61_out, nand_61_out);
endmodule
